// Logisim project calculadora-4-bits.circ as structural Verilog
module meia_soma (
  input  A,
  input  B,
  output saida,
  output vai_1
);

  xor xor_1 (saida, A, B);
  and and_1 (vai_1, B, A);
endmodule

module somador_completo (
  input  Ci0,
  input  A0,
  input  B0,
  output S0,
  output Co0
);

  wire s0_vai_1, s1_saida, s1_vai_1;

  meia_soma s1 (.A(A0), .B(B0), .saida(s1_saida), .vai_1(s1_vai_1));
  meia_soma u_s0 (.A(s1_saida), .B(Ci0), .saida(S0), .vai_1(s0_vai_1));
  or or_1 (Co0, s1_vai_1, s0_vai_1);
endmodule

module calculadora_4_bits (
  input  A0,
  input  A1,
  input  Carry_In,
  input  A2,
  input  A3,
  input  B0,
  input  B1,
  input  B2,
  input  B3,
  output S0,
  output S1,
  output S2,
  output S3,
  output overflow,
  output Carry_out
);

  Hex_Digit_Display hex_digit_display_1 (.value({A3, A2, A1, A0}));  // open: dp
  somador_4_bits somador_4_bits_1 (
    .A0(A0), .A1(A1), .A2(A2), .A3(A3), .B0(B0), .B1(B1), .B2(B2), .B3(B3), .Carry_in(Carry_In),
    .Carry_out(Carry_out), .S0(S0), .S1(S1), .S2(S2), .S3(S3), .Overflow(overflow));
  Hex_Digit_Display hex_digit_display_2 (.value({B3, B2, B1, B0}));  // open: dp
  Hex_Digit_Display hex_digit_display_3 (.value({S3, S2, S1, S0}));  // open: dp
endmodule

module somador_4_bits (
  input  Carry_in,
  input  A0,
  input  A1,
  input  A2,
  input  A3,
  input  B0,
  input  B1,
  input  B2,
  input  B3,
  output S0,
  output S1,
  output S2,
  output S3,
  output Carry_out,
  output Overflow
);

  wire somador_completo_1_co0, somador_completo_2_co0, somador_completo_3_co0;

  somador_completo somador_completo_1 (.A0(A0), .B0(B0), .Ci0(Carry_in), .S0(S0), .Co0(somador_completo_1_co0));
  somador_completo somador_completo_2 (
    .A0(A1), .B0(B1), .Ci0(somador_completo_1_co0), .S0(S1), .Co0(somador_completo_2_co0));
  somador_completo somador_completo_3 (
    .A0(A2), .B0(B2), .Ci0(somador_completo_2_co0), .S0(S2), .Co0(somador_completo_3_co0));
  somador_completo somador_completo_4 (.A0(A3), .B0(B3), .Ci0(somador_completo_3_co0), .S0(S3), .Co0(Carry_out));
  xor xor_1 (Overflow, somador_completo_3_co0, Carry_out);
endmodule
