// Logisim project ula-4-bits.circ as structural Verilog: 4 circuits, main circuit main
module main (
  input  a,
  input  b,
  input  [1:0] in_3,
  output S0,
  output out_5
);

  wire and_1_out, not_1_out, or_1_out, somador_completo_1_s0;

  and and_1 (and_1_out, a, b);
  or or_1 (or_1_out, a, b);
  not not_1 (not_1_out, a);
  somador_completo somador_completo_1 (.A0(a), .B0(a), .Ci0(1'b0), .S0(somador_completo_1_s0), .Co0(out_5));
  Multiplexer #(.select(2), .enable("false")) multiplexer_1 (
    .in0(and_1_out), .in1(or_1_out), .in2(not_1_out), .in3(somador_completo_1_s0), .out(S0), .sel(in_3));

  // Notes on the sheet:
  //   Carry in
endmodule

module meia_soma (
  input  A,
  input  B,
  output saida,
  output vai_1
);

  xor xor_1 (saida, A, B);
  and and_1 (vai_1, B, A);
endmodule

module somador_completo (
  input  Ci0,
  input  A0,
  input  B0,
  output S0,
  output Co0
);

  wire s0_vai_1, s1_saida, s1_vai_1;

  meia_soma s1 (.A(A0), .B(B0), .saida(s1_saida), .vai_1(s1_vai_1));
  meia_soma u_s0 (.A(s1_saida), .B(Ci0), .saida(S0), .vai_1(s0_vai_1));
  or or_1 (Co0, s1_vai_1, s0_vai_1);
endmodule

module ula_4_bits (
  input  A0,
  input  A1,
  input  A2,
  input  A3,
  input  B0,
  input  B1,
  input  B2,
  input  B3,
  input  Carry_In
);
endmodule
