// Logisim project somador-4-bits.circ as structural Verilog
module meia_soma (
  input  A,
  input  B,
  output vem_1,
  output vai_1
);

  xor xor_1 (vem_1, A, B);
  and and_1 (vai_1, B, A);
endmodule

module somador_completo (
  input  A,
  input  B,
  output S,
  output vai_1
);

  wire meia_soma_1_vai_1, meia_soma_1_vem_1, meia_soma_2_vai_1;

  meia_soma meia_soma_1 (.A(A), .B(B), .vem_1(meia_soma_1_vem_1), .vai_1(meia_soma_1_vai_1));
  meia_soma meia_soma_2 (.A(meia_soma_1_vem_1), .B(meia_soma_1_vai_1), .vem_1(S), .vai_1(meia_soma_2_vai_1));
  and and_1 (vai_1, meia_soma_1_vai_1, meia_soma_2_vai_1);
endmodule

module somador_4_bits (
  input  in_1,
  input  in_2,
  input  in_3,
  input  in_4,
  input  in_5,
  input  in_6,
  input  in_7,
  input  in_8,
  output out_9,
  output out_10,
  output out_11,
  output out_12
);

  somador_completo somador_completo_1 (.A(in_1), .B(in_2), .S(out_9));  // open: vai_1
  somador_completo somador_completo_2 (.A(in_3), .B(in_4), .S(out_10));  // open: vai_1
  somador_completo somador_completo_3 (.A(in_5), .B(in_6), .S(out_11));  // open: vai_1
  somador_completo somador_completo_4 (.A(in_7), .B(in_8), .S(out_12));  // open: vai_1
endmodule
